# Fritzing sketch wemos (saved by Fritzing 0.9.3b)

parts:
  WeMos_D1_Mini1 = WeMos D1 Mini
  U1 = Module 4 Relais 5V [package="Module 4 Relais 5V"]
  S1 = Pushbutton [package="[SMD]"]
  S2 = Pushbutton [package="[SMD]"]
  S3 = Pushbutton [package="[SMD]"]
  S4 = Pushbutton [package="[SMD]"]

nets:
  5V: WeMos_D1_Mini1.5V, U1.VCC
  N1: WeMos_D1_Mini1.D1, S4.Pin_1
  N2: WeMos_D1_Mini1.D2, S3.Pin_1
  N3: WeMos_D1_Mini1.D3, S2.Pin_1, S2.Pin_2
  N4: WeMos_D1_Mini1.D4, S1.Pin_1, S1.Pin_2
  N5: WeMos_D1_Mini1.D5, U1.IN4
  N6: WeMos_D1_Mini1.D6, U1.IN3
  N7: WeMos_D1_Mini1.D7, U1.IN2
  N8: WeMos_D1_Mini1.D8, U1.IN1
  N9: WeMos_D1_Mini1.G, U1.GND, S1.Pin_3, S1.Pin_4, S2.Pin_3, S2.Pin_4, S3.Pin_3, S3.Pin_4, S4.Pin_3, S4.Pin_4
  N10: U1.JD-VCC, U1.VCC2

custom parts:
  Module 4 Relais 5V: Module 4 Relais 5V 4x SPD-06VDC-SD-C
